# Fritzing sketch Partie_Capteur (saved by Fritzing 0.9.3b)
breadboards: 1

parts:
  Composant1 = Arduino Mega 2560 (Rev3)
  Bluetooth_Site_Web_et_Afficheurs = Bluetooth HC-05 Macho
  Bluetooth_Application = Bluetooth HC-05 Macho
  BMP_180 = Adafruit BMP180

nets:
  N1: Composant1.D21/SCL, BMP_180.SCL
  N2: Composant1.D20/SDA, BMP_180.SDA
  N3: Composant1.D19/RX1, Bluetooth_Site_Web_et_Afficheurs.TXD
  N4: Composant1.D18/TX1, Bluetooth_Site_Web_et_Afficheurs.RXD
  N5: Composant1.D17_PWM/RX2, Bluetooth_Application.TXD
  N6: Composant1.D16_PWM/TX2, Bluetooth_Application.RXD
  3V3: Composant1.3V3, BMP_180.+3V3
  5V: Composant1.5V, Bluetooth_Site_Web_et_Afficheurs.VCC, BMP_180.+5V
  GND: Composant1.GND, Bluetooth_Application.GND, BMP_180.GND

custom parts:
  Adafruit BMP180: This precision sensor from Bosch is the best low-cost sensing solution for measuring barometric pressure and temperature. Because pressure changes with altitude you can also use it as an altimeter! The sensor is soldered onto a PCB with a 3.3V regulator, I2C level shifter and pull-up resistors on the I2C pins. The BMP180 is the next-generation of sensors from Bosch, and replaces the BMP085.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
